// Logisim project FPA.circ as structural Verilog: 1 circuit, main circuit main
module main (
  input  [31:0] A,
  input  [31:0] B,
  output OverFlow,
  output UnderFlow
);

  wire inputhandler_1_larger_sign, inputhandler_1_smaller_sign;
  wire [8:0] inputhandler_1_larger_exponant, main_2_normalizedexponent;
  wire [31:0] inputhandler_1_larger_fraction, inputhandler_1_shifted_small_fraction,
       main_1_output_of_whole_adder, main_2_normalizedsignificand, main_3_rounded_significant;

  InputHandler inputhandler_1 (
    .InputA(A), .InputB(B), .Larger_Exponant(inputhandler_1_larger_exponant),
    .Larger_Fraction(inputhandler_1_larger_fraction), .Larger_Sign(inputhandler_1_larger_sign),
    .Shifted_Small_Fraction(inputhandler_1_shifted_small_fraction), .Smaller_sign(inputhandler_1_smaller_sign));  // open: out_5, Exponant_Difference, Samller_Fraction
  Adder_main main_1 (
    .A(inputhandler_1_larger_fraction), .B(inputhandler_1_shifted_small_fraction),
    .SIGNA(inputhandler_1_larger_sign), .SIGNB(inputhandler_1_smaller_sign),
    .OUTPUT_OF_WHOLE_ADDER(main_1_output_of_whole_adder));  // open: out_5, OUTPUTSIGN
  Normalizer_main main_2 (
    .Exponent_Input(inputhandler_1_larger_exponant), .Significand_Input(main_1_output_of_whole_adder),
    .UnderFlow(UnderFlow), .OverFlow(OverFlow), .NormalizedExponent(main_2_normalizedexponent),
    .NormalizedSignificand(main_2_normalizedsignificand));
  Rounder_main main_3 (.in_1(main_2_normalizedsignificand), .ROUNDED_SIGNIFICANT(main_3_rounded_significant));
endmodule
